// Logisim project Project.circ as structural Verilog: 14 circuits, main circuit main
// CPU
module main (
  output Cout,
  output Overflow
);

  wire ALU_zero_check, and_1_out, clock_1_out, control_unit_1_alusrc, control_unit_1_branch,
       control_unit_1_memread, control_unit_1_memtoreg, control_unit_1_memwrite, control_unit_1_regdst,
       control_unit_1_regwrite, Reset_out;
  wire [2:0] multiplexer_1_out;
  wire [3:0] alu_control_1_operation;
  wire [15:0] adder_1_out, adder_2_out, ALU_result, bit_extender_1_out, multiplexer_2_out, multiplexer_3_out,
       multiplexer_4_out, PC_q, ram_1_data, register_file_1_data01, register_file_1_data02, rom_1_data;

  Counter #(.width(16), .max('hffff), .trigger("falling")) PC (
    .load(1'b1), .D(multiplexer_3_out), .count(1'b0), .Q(PC_q), .clk(clock_1_out), .clr(Reset_out));  // open: carry
  Button Reset (.out(Reset_out));
  Clock clock_1 (.out(clock_1_out));
  Adder #(.width(16)) adder_1 (.a(PC_q), .b(16'h1), .out(adder_1_out));  // open: cin, cout
  ROM #(.addrWidth(16), .dataWidth(16)) rom_1 (.addr(PC_q), .data(rom_1_data));  // open: sel
  Control_unit control_unit_1 (
    .in_1(rom_1_data[15:12]), .RegDST(control_unit_1_regdst), .RegWrite(control_unit_1_regwrite),
    .ALUSRC(control_unit_1_alusrc), .MemRead(control_unit_1_memread), .MemWrite(control_unit_1_memwrite),
    .MemToReg(control_unit_1_memtoreg), .Branch(control_unit_1_branch));
  ALU_control alu_control_1 (.Opcode(rom_1_data[15:12]), .Operation(alu_control_1_operation));
  Multiplexer #(.width(3), .enable("false")) multiplexer_1 (
    .in0(rom_1_data[8:6]), .in1(rom_1_data[5:3]), .out(multiplexer_1_out), .sel(control_unit_1_regdst));
  assign bit_extender_1_out = {{10{rom_1_data[5]}}, rom_1_data[5:0]};  // Bit_Extender bit_extender_1
  Register_File register_file_1 (
    .Data_IN(multiplexer_4_out), .Data01(register_file_1_data01), .Data02(register_file_1_data02),
    .RD(multiplexer_1_out), .RS(rom_1_data[11:9]), .RT(rom_1_data[8:6]), .Clock(clock_1_out),
    .RegWrite(control_unit_1_regwrite));
  Multiplexer #(.width(16), .enable("false")) multiplexer_2 (
    .in0(register_file_1_data02), .in1(bit_extender_1_out), .out(multiplexer_2_out),
    .sel(control_unit_1_alusrc));
  _16_Bit_alu ALU (
    .ALU_Control(alu_control_1_operation), .B(multiplexer_2_out), .A(register_file_1_data01),
    .Shift_amt(rom_1_data[2:0]), .Result(ALU_result), .Cout(Cout), .Zero_check(ALU_zero_check),
    .Overflow(Overflow));
  Adder #(.width(16)) adder_2 (.a(adder_1_out), .b(bit_extender_1_out), .out(adder_2_out), .cin(1'b0));  // open: cout
  Multiplexer #(.width(16), .enable("false")) multiplexer_3 (
    .in0(adder_1_out), .in1(adder_2_out), .out(multiplexer_3_out), .sel(and_1_out));
  and and_1 (and_1_out, control_unit_1_branch, ALU_zero_check);
  RAM #(.addrWidth(16), .dataWidth(16), .bus("separate")) ram_1 (
    .addr(ALU_result), .din(register_file_1_data02), .data(ram_1_data), .str(control_unit_1_memwrite),
    .clk(clock_1_out), .ld(control_unit_1_memread));  // open: sel, clr
  Multiplexer #(.width(16), .enable("false")) multiplexer_4 (
    .in0(ram_1_data), .in1(ALU_result), .out(multiplexer_4_out), .sel(control_unit_1_memtoreg));

  // Notes on the sheet:
  //   Instruction memory
  //   contents of rom_1 (hex, n*v repeats v):
  //   b04b b081 b0c0 c283 3698 b481 c03c 2100 18c0
  //   Control Unit
  //   ALU Control
  //   Register file
  //   Data memory
endmodule

module Register_File (
  input  RegWrite,
  input  [15:0] Data_IN,
  input  [2:0] RS,
  input  [2:0] RT,
  input  Clock,
  input  [2:0] RD,
  output [15:0] Data01,
  output [15:0] Data02
);

  wire and_1_out, and_2_out, and_3_out, and_4_out, and_5_out, and_6_out, and_7_out, and_8_out,
       decoder_1_out0, decoder_1_out1, decoder_1_out2, decoder_1_out3, decoder_1_out4, decoder_1_out5,
       decoder_1_out6, decoder_1_out7;
  wire [15:0] register_1_q, register_2_q, register_3_q, register_4_q, register_5_q, register_6_q,
       register_7_q, register_8_q;

  Decoder #(.select(3)) decoder_1 (
    .out0(decoder_1_out0), .out1(decoder_1_out1), .out2(decoder_1_out2), .out3(decoder_1_out3),
    .out4(decoder_1_out4), .out5(decoder_1_out5), .out6(decoder_1_out6), .out7(decoder_1_out7), .sel(RD));  // open: en
  and and_1 (and_1_out, RegWrite, decoder_1_out0);
  and and_2 (and_2_out, RegWrite, decoder_1_out1);
  and and_3 (and_3_out, decoder_1_out2, RegWrite);
  and and_4 (and_4_out, decoder_1_out3, RegWrite);
  and and_5 (and_5_out, decoder_1_out4, RegWrite);
  and and_6 (and_6_out, decoder_1_out5, RegWrite);
  and and_7 (and_7_out, RegWrite, decoder_1_out6);
  and and_8 (and_8_out, decoder_1_out7, RegWrite);
  Register #(.width(16)) register_1 (.D({16{1'b0}}), .en(and_1_out), .Q(register_1_q), .clk(Clock));  // open: clr
  Register #(.width(16)) register_2 (.D(Data_IN), .en(and_2_out), .Q(register_2_q), .clk(Clock));  // open: clr
  Register #(.width(16)) register_3 (.D(Data_IN), .en(and_3_out), .Q(register_3_q), .clk(Clock));  // open: clr
  Register #(.width(16)) register_4 (.D(Data_IN), .en(and_4_out), .Q(register_4_q), .clk(Clock));  // open: clr
  Register #(.width(16)) register_5 (.D(Data_IN), .en(and_5_out), .Q(register_5_q), .clk(Clock));  // open: clr
  Register #(.width(16)) register_6 (.D(Data_IN), .en(and_6_out), .Q(register_6_q), .clk(Clock));  // open: clr
  Register #(.width(16)) register_7 (.D(Data_IN), .en(and_7_out), .Q(register_7_q), .clk(Clock));  // open: clr
  Register #(.width(16)) register_8 (.D(Data_IN), .en(and_8_out), .Q(register_8_q), .clk(Clock));  // open: clr
  Multiplexer #(.select(3), .width(16)) multiplexer_1 (
    .in0(register_1_q), .in1(register_2_q), .in2(register_3_q), .in3(register_4_q), .in4(register_5_q),
    .in5(register_6_q), .in6(register_7_q), .in7(register_8_q), .out(Data02), .sel(RT));  // open: en
  Multiplexer #(.select(3), .width(16)) multiplexer_2 (
    .in0(register_1_q), .in1(register_2_q), .in2(register_3_q), .in3(register_4_q), .in4(register_5_q),
    .in5(register_6_q), .in6(register_7_q), .in7(register_8_q), .out(Data01), .sel(RS));  // open: en
endmodule

module _16_Bit_alu (
  input  [3:0] ALU_Control,
  input  [15:0] A,
  input  [15:0] B,
  input  [2:0] Shift_amt,
  output Zero_check,
  output Cout,
  output [15:0] Result,
  output Overflow
);

  wire [3:0] bit_extender_1_out;
  wire [15:0] arithmetic_alu_1_result, demultiplexer_1_out0, demultiplexer_1_out1, shifter_1_out_4;

  Demultiplexer #(.width(16), .enable("false")) demultiplexer_1 (
    .out0(demultiplexer_1_out0), .out1(demultiplexer_1_out1), .in(A), .sel(ALU_Control[3]));
  assign bit_extender_1_out = {{1{1'b0}}, Shift_amt};  // Bit_Extender bit_extender_1
  Arithmetic_ALU arithmetic_alu_1 (
    .A(demultiplexer_1_out0), .B(B), .Zero(Zero_check), .Result(arithmetic_alu_1_result), .Cout(Cout),
    .Overflow(Overflow), .Operation(ALU_Control[2:1]), .B_inverter(ALU_Control[0]));
  Shifter shifter_1 (
    .A(demultiplexer_1_out1), .Shmt(bit_extender_1_out), .out_4(shifter_1_out_4), .Operation(ALU_Control[2:1]));
  Multiplexer #(.width(16)) multiplexer_1 (
    .in0(arithmetic_alu_1_result), .in1(shifter_1_out_4), .out(Result), .sel(ALU_Control[3]));  // open: en
endmodule

module _1_bit_alu (
  input  A,
  input  B,
  input  [1:0] Data_operation,
  input  Cin,
  input  B_inverter,
  output Result,
  output Cout
);

  wire adder_1_out, and_1_out, multiplexer_1_out, not_1_out, or_1_out;

  Multiplexer multiplexer_1 (.in0(B), .in1(not_1_out), .out(multiplexer_1_out), .sel(B_inverter));  // open: en
  not not_1 (not_1_out, B);
  and and_1 (and_1_out, A, B);
  or or_1 (or_1_out, A, B);
  Adder #(.width(1)) adder_1 (.a(A), .b(multiplexer_1_out), .out(adder_1_out), .cin(Cin), .cout(Cout));
  Multiplexer #(.select(2)) multiplexer_2 (
    .in0(and_1_out), .in1(or_1_out), .in2(adder_1_out), .in3(1'b0), .out(Result), .sel(Data_operation));  // open: en
endmodule

// LSB ALU
module _1_bit_ALU__LSB (
  input  A,
  input  B,
  input  [1:0] Data_operation,
  input  Cin,
  input  B_inverter,
  input  A_less_than_B,
  output Result,
  output Cout
);

  wire adder_1_out, and_1_out, multiplexer_1_out, not_1_out, or_1_out;

  Multiplexer multiplexer_1 (.in0(B), .in1(not_1_out), .out(multiplexer_1_out), .sel(B_inverter));  // open: en
  not not_1 (not_1_out, B);
  and and_1 (and_1_out, A, B);
  or or_1 (or_1_out, A, B);
  Adder #(.width(1)) adder_1 (.a(A), .b(multiplexer_1_out), .out(adder_1_out), .cin(Cin), .cout(Cout));
  Multiplexer #(.select(2)) multiplexer_2 (
    .in0(and_1_out), .in1(or_1_out), .in2(adder_1_out), .in3(A_less_than_B), .out(Result),
    .sel(Data_operation));  // open: en
endmodule

// MSB ALU
module _1_bit_ALU__MSB (
  input  A,
  input  B,
  input  [1:0] Data_operation,
  input  Cin,
  input  B_inverter,
  output Result,
  output Cout,
  output Set_on_less_than
);

  wire and_1_out, multiplexer_1_out, not_1_out, or_1_out;

  Multiplexer multiplexer_1 (.in0(B), .in1(not_1_out), .out(multiplexer_1_out), .sel(B_inverter));  // open: en
  not not_1 (not_1_out, B);
  and and_1 (and_1_out, A, B);
  or or_1 (or_1_out, A, B);
  Adder #(.width(1)) adder_1 (.a(A), .b(multiplexer_1_out), .out(Set_on_less_than), .cin(Cin), .cout(Cout));
  Multiplexer #(.select(2)) multiplexer_2 (
    .in0(and_1_out), .in1(or_1_out), .in2(Set_on_less_than), .in3(1'b0), .out(Result), .sel(Data_operation));  // open: en
endmodule

// OF
module Overflow (
  input  in_1,
  input  in_2,
  output out_3
);

  xor xor_1 (out_3, in_1, in_2);
endmodule

// A.ALU
module Arithmetic_ALU (
  input  [15:0] A,
  input  B_inverter,
  input  [1:0] Operation,
  input  [15:0] B,
  output Zero,
  output [15:0] Result,
  output Cout,
  output Overflow
);

  wire n1_bit_alu_1_cout, n1_bit_alu_2_cout, n1_bit_alu_3_cout, n1_bit_alu_4_cout, n1_bit_alu_5_cout,
       n1_bit_alu_6_cout, n1_bit_alu_7_cout, n1_bit_alu_8_cout, n1_bit_alu_9_cout, n1_bit_alu_10_cout,
       n1_bit_alu_11_cout, n1_bit_alu_12_cout, n1_bit_alu_13_cout, n1_bit_alu_14_cout, n1_bit_alu_lsb_1_cout,
       n1_bit_alu_msb_1_set_on_less_than;

  _1_bit_ALU__LSB u_1_bit_alu_lsb_1 (
    .A(A[0]), .B(B[0]), .A_less_than_B(n1_bit_alu_msb_1_set_on_less_than), .Result(Result[0]),
    .Cout(n1_bit_alu_lsb_1_cout), .B_inverter(B_inverter), .Cin(B_inverter), .Data_operation(Operation));
  _1_bit_alu u_1_bit_alu_1 (
    .A(A[1]), .B(B[1]), .Result(Result[1]), .Cout(n1_bit_alu_1_cout), .Cin(n1_bit_alu_lsb_1_cout),
    .Data_operation(Operation), .B_inverter(B_inverter));
  _1_bit_alu u_1_bit_alu_2 (
    .A(A[2]), .B(B[2]), .Result(Result[2]), .Cout(n1_bit_alu_2_cout), .Cin(n1_bit_alu_1_cout),
    .Data_operation(Operation), .B_inverter(B_inverter));
  _1_bit_alu u_1_bit_alu_3 (
    .A(A[3]), .B(B[3]), .Result(Result[3]), .Cout(n1_bit_alu_3_cout), .Cin(n1_bit_alu_2_cout),
    .Data_operation(Operation), .B_inverter(B_inverter));
  _1_bit_alu u_1_bit_alu_4 (
    .A(A[4]), .B(B[4]), .Result(Result[4]), .Cout(n1_bit_alu_4_cout), .Cin(n1_bit_alu_3_cout),
    .Data_operation(Operation), .B_inverter(B_inverter));
  _1_bit_alu u_1_bit_alu_5 (
    .A(A[5]), .B(B[5]), .Result(Result[5]), .Cout(n1_bit_alu_5_cout), .Cin(n1_bit_alu_4_cout),
    .Data_operation(Operation), .B_inverter(B_inverter));
  _1_bit_alu u_1_bit_alu_6 (
    .A(A[6]), .B(B[6]), .Result(Result[6]), .Cout(n1_bit_alu_6_cout), .Cin(n1_bit_alu_5_cout),
    .Data_operation(Operation), .B_inverter(B_inverter));
  _1_bit_alu u_1_bit_alu_7 (
    .A(A[7]), .B(B[7]), .Result(Result[7]), .Cout(n1_bit_alu_7_cout), .Cin(n1_bit_alu_6_cout),
    .Data_operation(Operation), .B_inverter(B_inverter));
  _1_bit_alu u_1_bit_alu_8 (
    .A(A[8]), .B(B[8]), .Result(Result[8]), .Cout(n1_bit_alu_8_cout), .Cin(n1_bit_alu_7_cout),
    .Data_operation(Operation), .B_inverter(B_inverter));
  _1_bit_alu u_1_bit_alu_9 (
    .A(A[9]), .B(B[9]), .Result(Result[9]), .Cout(n1_bit_alu_9_cout), .Cin(n1_bit_alu_8_cout),
    .Data_operation(Operation), .B_inverter(B_inverter));
  _1_bit_alu u_1_bit_alu_10 (
    .A(A[10]), .B(B[10]), .Result(Result[10]), .Cout(n1_bit_alu_10_cout), .Cin(n1_bit_alu_9_cout),
    .Data_operation(Operation), .B_inverter(B_inverter));
  _1_bit_alu u_1_bit_alu_11 (
    .A(A[11]), .B(B[11]), .Result(Result[11]), .Cout(n1_bit_alu_11_cout), .Cin(n1_bit_alu_10_cout),
    .Data_operation(Operation), .B_inverter(B_inverter));
  _1_bit_alu u_1_bit_alu_12 (
    .A(A[12]), .B(B[12]), .Result(Result[12]), .Cout(n1_bit_alu_12_cout), .Cin(n1_bit_alu_11_cout),
    .Data_operation(Operation), .B_inverter(B_inverter));
  _1_bit_alu u_1_bit_alu_13 (
    .A(A[13]), .B(B[13]), .Result(Result[13]), .Cout(n1_bit_alu_13_cout), .Cin(n1_bit_alu_12_cout),
    .Data_operation(Operation), .B_inverter(B_inverter));
  _1_bit_alu u_1_bit_alu_14 (
    .A(A[14]), .B(B[14]), .Result(Result[14]), .Cout(n1_bit_alu_14_cout), .Cin(n1_bit_alu_13_cout),
    .Data_operation(Operation), .B_inverter(B_inverter));
  _1_bit_ALU__MSB u_1_bit_alu_msb_1 (
    .A(A[15]), .B(B[15]), .Result(Result[15]), .Cout(Cout),
    .Set_on_less_than(n1_bit_alu_msb_1_set_on_less_than), .B_inverter(B_inverter), .Cin(n1_bit_alu_14_cout),
    .Data_operation(Operation));
  Overflow overflow_1 (.in_1(n1_bit_alu_14_cout), .in_2(Cout), .out_3(Overflow));
  nor nor_1 (Zero, Result[0], Result[1], Result[2], Result[3], Result[4], Result[5], Result[6], Result[7], Result[8], Result[9], Result[10], Result[11], Result[12], Result[13], Result[14], Result[15]);
endmodule

// L.ALU
module Shifter (
  input  [15:0] A,
  input  [1:0] Operation,
  input  [3:0] Shmt,
  output [15:0] out_4
);

  wire [15:0] demultiplexer_1_out0, demultiplexer_1_out1, demultiplexer_1_out2, not_1_out_2, shifter_1_out,
       shifter_2_out;

  Demultiplexer #(.select(2), .width(16), .enable("false")) demultiplexer_1 (
    .out0(demultiplexer_1_out0), .out1(demultiplexer_1_out1), .out2(demultiplexer_1_out2), .in(A),
    .sel(Operation));  // open: out3
  Shifter_part #(.width(16)) shifter_1 (.in(demultiplexer_1_out0), .\dist (Shmt), .out(shifter_1_out));
  Shifter_part #(.width(16), .shift("lr")) shifter_2 (.in(demultiplexer_1_out1), .\dist (Shmt), .out(shifter_2_out));
  NOT not_1 (.in_1(demultiplexer_1_out2), .out_2(not_1_out_2));
  Multiplexer #(.select(2), .width(16), .enable("false")) multiplexer_1 (
    .in0(shifter_1_out), .in1(shifter_2_out), .in2(not_1_out_2), .out(out_4), .sel(Operation));  // open: in3
endmodule

module NOT (
  input  [15:0] in_1,
  output [15:0] out_2
);

  not not_1 (out_2[0], in_1[0]);
  not not_2 (out_2[1], in_1[1]);
  not not_3 (out_2[2], in_1[2]);
  not not_4 (out_2[3], in_1[3]);
  not not_5 (out_2[4], in_1[4]);
  not not_6 (out_2[5], in_1[5]);
  not not_7 (out_2[6], in_1[6]);
  not not_8 (out_2[7], in_1[7]);
  not not_9 (out_2[8], in_1[8]);
  not not_10 (out_2[9], in_1[9]);
  not not_11 (out_2[10], in_1[10]);
  not not_12 (out_2[11], in_1[11]);
  not not_13 (out_2[12], in_1[12]);
  not not_14 (out_2[13], in_1[13]);
  not not_15 (out_2[14], in_1[14]);
  not not_16 (out_2[15], in_1[15]);
endmodule

module DATA_memory (
  input  [15:0] Address,
  input  MemRead,
  input  MemWrite,
  input  [15:0] Write_data,
  output [15:0] Result
);
endmodule

module Control_unit (
  input  [3:0] in_1,
  output RegDST,
  output RegWrite,
  output ALUSRC,
  output MemRead,
  output MemWrite,
  output MemToReg,
  output Branch
);

  wire and_1_out, and_2_out, and_3_out, and_4_out, and_5_out, and_6_out, and_7_out, and_8_out, not_1_out,
       not_2_out, not_3_out, not_4_out;

  not not_1 (not_1_out, in_1[3]);
  not not_2 (not_2_out, in_1[1]);
  not not_3 (not_3_out, in_1[0]);
  not not_4 (not_4_out, in_1[2]);
  and and_1 (and_1_out, not_1_out, in_1[0]);
  and and_2 (and_2_out, in_1[3], not_2_out);
  and and_3 (and_3_out, in_1[3], not_4_out);
  and and_4 (and_4_out, not_1_out, not_3_out);
  and and_5 (and_5_out, in_1[2], in_1[0]);
  and and_6 (and_6_out, in_1[3], in_1[1]);
  and and_7 (and_7_out, not_4_out, not_2_out);
  and and_8 (and_8_out, not_4_out, not_3_out);
  or or_1 (MemToReg, in_1[3], in_1[2], in_1[1]);
  or or_2 (RegDST, and_1_out, and_2_out, in_1[2]);
  or or_3 (RegWrite, and_3_out, and_4_out, in_1[1], and_5_out);
  or or_4 (ALUSRC, and_6_out, and_7_out, and_8_out);
  and and_9 (MemRead, not_1_out, not_4_out, not_2_out, not_3_out);
  and and_10 (MemWrite, not_1_out, not_4_out, not_2_out, in_1[0]);
  and and_11 (Branch, in_1[3], in_1[2], not_2_out, not_3_out);

  // Notes on the sheet:
  //   B
  //   C
  //   A
  //   A
  //   B
  //   C
  //   D
  //   D
endmodule

module Data_path (
  output Cout,
  output Overflow
);

  wire ALU_zero_check, and_1_out, clock_1_out, control_unit_1_alusrc, control_unit_1_branch,
       control_unit_1_memread, control_unit_1_memtoreg, control_unit_1_memwrite, control_unit_1_regdst,
       control_unit_1_regwrite, Reset_out;
  wire [2:0] multiplexer_1_out;
  wire [2:2] undriven;
  wire [3:0] alu_control_1_operation;
  wire [15:0] adder_1_out, adder_2_out, ALU_result, bit_extender_1_out, multiplexer_2_out, multiplexer_3_out,
       multiplexer_4_out, PC_q, ram_1_data, register_file_1_data01, register_file_1_data02, rom_1_data,
       shifter_1_out;

  Counter #(.width(16), .max('hffff)) PC (
    .D(multiplexer_3_out), .Q(PC_q), .clk(clock_1_out), .clr(Reset_out));  // open: load, count, carry
  Button Reset (.out(Reset_out));
  Clock clock_1 (.out(clock_1_out));
  Adder #(.width(16)) adder_1 (.a(PC_q), .b(16'h1), .out(adder_1_out));  // open: cin, cout
  ROM #(.addrWidth(16), .dataWidth(16)) rom_1 (.addr(PC_q), .data(rom_1_data));  // open: sel
  Control_unit control_unit_1 (
    .in_1(rom_1_data[15:12]), .RegDST(control_unit_1_regdst), .RegWrite(control_unit_1_regwrite),
    .ALUSRC(control_unit_1_alusrc), .MemRead(control_unit_1_memread), .MemWrite(control_unit_1_memwrite),
    .MemToReg(control_unit_1_memtoreg), .Branch(control_unit_1_branch));
  ALU_control alu_control_1 (.Opcode(rom_1_data[15:12]), .Operation(alu_control_1_operation));
  Multiplexer #(.width(3), .enable("false")) multiplexer_1 (
    .in0(rom_1_data[8:6]), .in1(rom_1_data[5:3]), .out(multiplexer_1_out), .sel(control_unit_1_regdst));
  assign bit_extender_1_out = {{10{1'b0}}, rom_1_data[5:0]};  // Bit_Extender bit_extender_1
  Register_File register_file_1 (
    .Data_IN(multiplexer_4_out), .Data01(register_file_1_data01), .Data02(register_file_1_data02),
    .RD(multiplexer_1_out), .RS(rom_1_data[11:9]), .RT(rom_1_data[8:6]), .Clock(clock_1_out),
    .RegWrite(control_unit_1_regwrite));
  Multiplexer #(.width(16), .enable("false")) multiplexer_2 (
    .in0(register_file_1_data02), .in1(bit_extender_1_out), .out(multiplexer_2_out),
    .sel(control_unit_1_alusrc));
  Shifter_part #(.width(16)) shifter_1 (.in(bit_extender_1_out), .\dist (4'b0010), .out(shifter_1_out));
  _16_Bit_alu ALU (
    .ALU_Control(alu_control_1_operation), .B(multiplexer_2_out), .A(register_file_1_data01),
    .Shift_amt({undriven[2], rom_1_data[2:1]}), .Result(ALU_result), .Cout(Cout),
    .Zero_check(ALU_zero_check), .Overflow(Overflow));
  Adder #(.width(16)) adder_2 (.a(adder_1_out), .b(shifter_1_out), .out(adder_2_out));  // open: cin, cout
  Multiplexer #(.width(16), .enable("false")) multiplexer_3 (
    .in0(adder_1_out), .in1(adder_2_out), .out(multiplexer_3_out), .sel(and_1_out));
  and and_1 (and_1_out, control_unit_1_branch, ALU_zero_check);
  RAM #(.addrWidth(16), .dataWidth(16), .bus("separate")) ram_1 (
    .addr(ALU_result), .din(register_file_1_data02), .data(ram_1_data), .str(control_unit_1_memwrite),
    .clk(clock_1_out), .ld(control_unit_1_memread));  // open: sel, clr
  Multiplexer #(.width(16), .enable("false")) multiplexer_4 (
    .in0(ram_1_data), .in1(ALU_result), .out(multiplexer_4_out), .sel(control_unit_1_memtoreg));
  // Pins of 2 and 3 bits meet at {undriven[2], rom_1_data[2:1]}

  // Notes on the sheet:
  //   Instruction memory
  //   Control Unit
  //   ALU Control
  //   Register file
  //   Data memory
endmodule

module ALU_control (
  input  [3:0] Opcode,
  output [3:0] Operation
);

  Multiplexer #(.select(4), .width(4), .enable("false")) multiplexer_1 (
    .in0(4'b0100), .in1(4'b0100), .in2(4'b0100), .in3(4'b0100), .in4(4'b0101), .in5(4'b0000), .in6(4'b0010),
    .in7(4'b1100), .in8(4'b1000), .in9(4'b1010), .in10(4'b0010), .in11(4'b0100), .in12(4'b0101),
    .in13(4'b0111), .out(Operation), .sel(Opcode));  // open: in14, in15
endmodule
